# Fritzing sketch Pibot (saved by Fritzing 0.9.9b)
breadboards: 1

parts:
  M1 = gear-motor  # not connected
  M2 = gear-motor  # not connected
  MCU1 = Raspberry Pi Zero
  U1 = LCD-16X2 [package=lcd-16x2_noholes]  # not connected
  LCM1602_IIC1 = LCM1602 IIC [part_number="LCM1602 IIC" chip_label="LCM1602 IIC" package="DIP (Dual Inline) [THT]"]
  HC-SR04_Sensor_1 = HC-SR04 Ultrasonic Distance Sensor
  Enc1 = shaft encoder
  Enc3 = shaft encoder
  Part1 = Logic Level Converter

nets:
  VCC: MCU1.pin_2, MCU1.pin_4, LCM1602_IIC1.VCC, HC-SR04_Sensor_1.VCC, Enc3.VCC
  N1: MCU1.pin_5, LCM1602_IIC1.SCL
  GND: MCU1.pin_6, MCU1.pin_39, LCM1602_IIC1.GND, Enc1.GND, Enc3.GND, Part1.GND
  N2: MCU1.pin_7, LCM1602_IIC1.SDA
  N3: MCU1.pin_40, Enc1.OUT
  N4: Enc1.VCC, Part1.HV

custom parts:
  LCM1602 IIC: I2C-Module to use a 1602 or 2004 LCD on with the wire.h libory Serial LCD Modul
