# Fritzing sketch Untitled 3 (saved by Fritzing 0.9.9b)

parts:
  Mod1 = Raspberry Pi 4B
  U1 = LCD-16X2 [package=lcd-16x2_noholes]  # not connected
  LCM1602_IIC1 = LCM1602 IIC [part_number="LCM1602 IIC" chip_label="LCM1602 IIC" package="DIP (Dual Inline) [THT]"]

nets:
  5V: Mod1.5V, LCM1602_IIC1.VCC
  N1: Mod1.GPIO2, LCM1602_IIC1.SDA
  N2: Mod1.GPIO3, LCM1602_IIC1.SCL
  GND: Mod1.GND, LCM1602_IIC1.GND

custom parts:
  LCM1602 IIC: I2C-Module to use a 1602 or 2004 LCD on with the wire.h libory Serial LCD Modul
